// Logisim project smoothsort.circ as structural Verilog: 3 circuits, main circuit main
module main (
  input  RST,
  input  RIN,
  input  [3:0] RIN_SELECT,
  input  in_4,
  input  [3:0] ROUT_SELECT,
  input  ROUT,
  input  [6:0] in_7,
  input  BP,
  output BEOA,
  output BL2,
  output BCMP,
  output [3:0] RDST,
  output [3:0] RSRC,
  output [6:0] VAL,
  output [3:0] RLEFT,
  output [2:0] RRIGHT,
  output [1:0] BTYPE,
  output FLAG,
  output READ,
  output COUNT
);

  wire A1, ABIN, ABRES, ALUOUT, and_1_out, and_3_out, and_4_out, and_6_out, and_7_out, and_8_out, and_9_out,
       and_10_out, and_11_out, and_12_out, and_13_out, and_16_out, and_18_out, and_19_out, and_20_out,
       AP_CNT, AP_DIR, ARIN, ARITH, ARSTEP, B, BP_t, BTrue, CLK_out, comparator_1_eq, comparator_2_eq,
       comparator_2_gt, comparator_3_eq, comparator_3_gt, comparator_4_eq, comparator_4_gt, CREN, d_ff_1_q,
       demultiplexer_1_out0, demultiplexer_1_out1, demultiplexer_1_out2, demultiplexer_1_out3,
       demultiplexer_1_out4, demultiplexer_1_out5, demultiplexer_1_out6, demultiplexer_1_out7,
       demultiplexer_1_out8, demultiplexer_1_out9, demultiplexer_2_out0, HLT, HSP_CNT, HSP_DIR, LD_ST, LNK,
       MEM, MOV_L, nand_1_out, NOP, nor_2_out, nor_3_out, not_1_out, not_2_out, not_3_out, not_4_out,
       not_5_out, not_6_out, not_7_out, not_8_out, not_9_out, not_10_out, not_11_out, not_12_out, not_13_out,
       not_14_out, or_1_out, or_2_out, or_3_out, or_4_out, or_5_out, or_6_out, or_11_out, or_12_out,
       or_15_out, OUT, OUT_q, PC_CNT, pull_resistor_4_node, RDI, RDO, RET, RLC, RT, RVC, RW, STEP, W,
       xor_1_out, xor_2_out, xor_3_out;
  wire [0:0] pull_resistor_5_node;
  wire [1:0] S;
  wire [2:0] bit_extender_18_out;
  wire [3:0] bit_extender_15_out, bit_extender_16_out, bit_extender_17_out, bit_extender_19_out,
       bit_extender_20_out, bit_extender_23_out, controlled_buffer_1_out, controlled_buffer_4_out,
       controlled_buffer_11_out, controlled_buffer_12_out, controlled_buffer_14_out,
       controlled_buffer_15_out, controlled_buffer_16_out, RDST_t, RV;
  wire [6:0] AP_q, AR1_q, AR2_q, AR_q, ASR_q, bit_extender_1_out, bit_extender_2_out, bit_extender_3_out,
       bit_extender_5_out, bit_extender_6_out, bit_extender_7_out, bit_extender_8_out, bit_extender_22_out,
       CR_q, HSP_q, multiplexer_1_out, multiplexer_2_out, PC_q, RET_q, subtractor_1_out;
  wire [7:0] adder_1_out, ALUBUF_q, bit_extender_9_out, bit_extender_10_out, bit_extender_11_out,
       bit_extender_12_out, bit_extender_13_out, bit_extender_14_out, bit_extender_24_out,
       bit_extender_25_out, bit_extender_26_out, bit_extender_27_out, controlled_buffer_8_out,
       controlled_buffer_9_out, controlled_inverter_1_out, CROUT, multiplexer_3_out, multiplexer_4_out,
       multiplexer_7_out, OR1_q, OR2_q, PR1_q, PR2_q, RA_q, RB_q, RC_q, RD_q, subtractor_2_out,
       \мини_расческа1_1_out_2 , \мини_расческа1_1_out_3 ;
  wire [8:0] bit_extender_4_out;
  wire [11:0] rom_1_data;
  wire [15:0] counter_1_q, divider_1_out, divider_1_rem, divider_2_out, divider_2_rem, divider_3_out,
       divider_3_rem, divider_4_out, divider_4_rem, divider_5_rem, ram_1_data;
  wire [15:11] OP;

  assign controlled_buffer_1_out = in_4 ? RIN_SELECT : 4'bz;  // Controlled_Buffer controlled_buffer_1
  assign controlled_buffer_1_out = or_1_out ? 4'b1001 : 4'bz;  // Controlled_Buffer controlled_buffer_2
  or or_1 (or_1_out, BTrue, RT);
  assign controlled_buffer_1_out = RDI ? RDST_t : 4'bz;  // Controlled_Buffer controlled_buffer_3
  or or_2 (or_2_out, RT, RIN, BTrue, RDI);
  assign controlled_buffer_4_out = ROUT ? ROUT_SELECT : 4'bz;  // Controlled_Buffer controlled_buffer_4
  assign controlled_buffer_4_out = RVC ? RV : 4'bz;  // Controlled_Buffer controlled_buffer_5
  assign controlled_buffer_4_out = RDO ? RDST_t : 4'bz;  // Controlled_Buffer controlled_buffer_6
  assign controlled_buffer_4_out = RLC ? RLEFT : 4'bz;  // Controlled_Buffer controlled_buffer_7
  not not_1 (not_1_out, COUNT);
  Clock CLK (.out(CLK_out));
  or or_3 (or_3_out, RVC, RDO, RLC, ROUT);
  and and_1 (and_1_out, controlled_buffer_4_out[3], controlled_buffer_4_out[2], controlled_buffer_4_out[1]);
  xor xor_1 (xor_1_out, PC_CNT, BTrue);
  and and_2 (A1, not_1_out, MOV_L);
  and and_3 (and_3_out, MOV_L, COUNT);
  D_Flip_Flop d_ff_1 (.Q(d_ff_1_q), .preset(OUT_q), .reset(RST));  // open: clk, D, Qn, en
  not not_2 (not_2_out, BP_t);
  Demultiplexer #(.select(4), .disabled(0)) demultiplexer_1 (
    .out0(demultiplexer_1_out0), .out1(demultiplexer_1_out1), .out2(demultiplexer_1_out2),
    .out3(demultiplexer_1_out3), .out4(demultiplexer_1_out4), .out5(demultiplexer_1_out5),
    .out6(demultiplexer_1_out6), .out7(demultiplexer_1_out7), .out8(demultiplexer_1_out8),
    .out9(demultiplexer_1_out9), .out10(CREN), .in(or_2_out), .sel(controlled_buffer_1_out), .en(or_2_out));  // open: out11, out12, out13, out14, out15
  Pull_Resistor pull_resistor_1 (.node(controlled_buffer_1_out));
  Pull_Resistor pull_resistor_2 (.node(controlled_buffer_4_out));
  Multiplexer #(.width(7), .disabled(0)) multiplexer_1 (
    .in0(PC_q), .in1({RLEFT, RRIGHT[2:1], FLAG}), .out(multiplexer_1_out), .sel(BTrue), .en(1'b1));
  and and_4 (and_4_out, CLK_out, not_2_out);
  ROM #(.addrWidth(4), .dataWidth(12)) rom_1 (.addr({OP[15], MEM, S}), .data(rom_1_data));  // open: sel
  LED led_1 (.in(d_ff_1_q));
  not not_3 (not_3_out, d_ff_1_q);
  or or_4 (or_4_out, HSP_DIR, demultiplexer_1_out7);
  Bit_Extender #(.out_width(7)) bit_extender_1 (.in(controlled_buffer_9_out), .out(bit_extender_1_out));
  or or_5 (or_5_out, AP_DIR, demultiplexer_1_out8);
  Bit_Extender #(.out_width(7)) bit_extender_2 (.in(controlled_buffer_9_out), .out(bit_extender_2_out));
  Bit_Extender #(.out_width(7)) bit_extender_3 (.in(controlled_buffer_9_out), .out(bit_extender_3_out));
  not not_4 (not_4_out, PC_CNT);
  Bit_Extender #(.in_width(12), .out_width(9)) bit_extender_4 (.in(rom_1_data), .out(bit_extender_4_out));
  D_Flip_Flop u_OUT (.clk(and_4_out), .D(FLAG), .Q(OUT_q), .en(OUT), .reset(RST));  // open: Qn, preset
  Register OR1 (.D(RA_q), .en(OUT), .Q(OR1_q), .clk(and_4_out), .clr(RST));
  Register OR2 (.D(RB_q), .en(OUT), .Q(OR2_q), .clk(and_4_out), .clr(RST));
  Counter #(.width(16), .max('hffff)) counter_1 (
    .count(not_3_out), .Q(counter_1_q), .clk(and_4_out), .clr(RST));  // open: load, D, carry
  Register RA (.D(controlled_buffer_9_out), .en(demultiplexer_1_out0), .Q(RA_q), .clk(and_4_out), .clr(RST));
  Register RB (.D(controlled_buffer_9_out), .en(demultiplexer_1_out1), .Q(RB_q), .clk(and_4_out), .clr(RST));
  Register RC (.D(controlled_buffer_9_out), .en(demultiplexer_1_out2), .Q(RC_q), .clk(and_4_out), .clr(RST));
  Register RD (.D(controlled_buffer_9_out), .en(demultiplexer_1_out3), .Q(RD_q), .clk(and_4_out), .clr(RST));
  Bit_Extender #(.out_width(7)) bit_extender_5 (.in(controlled_buffer_9_out), .out(bit_extender_5_out));
  Register #(.width(7)) AR1 (.D(bit_extender_5_out), .en(demultiplexer_1_out4), .Q(AR1_q), .clk(and_4_out), .clr(RST));
  Bit_Extender #(.out_width(7)) bit_extender_6 (.in(controlled_buffer_9_out), .out(bit_extender_6_out));
  Register #(.width(7)) AR2 (.D(bit_extender_6_out), .en(demultiplexer_1_out5), .Q(AR2_q), .clk(and_4_out), .clr(RST));
  Bit_Extender #(.out_width(7)) bit_extender_7 (.in(controlled_buffer_9_out), .out(bit_extender_7_out));
  Register #(.width(7)) ASR (.D(bit_extender_7_out), .en(demultiplexer_1_out6), .Q(ASR_q), .clk(and_4_out), .clr(RST));
  Counter #(.width(7), .max('h7f)) HSP (
    .load(or_4_out), .D(bit_extender_1_out), .count(HSP_CNT), .Q(HSP_q), .clk(and_4_out), .clr(RST));  // open: carry
  Counter #(.width(7), .max('h7f)) AP (
    .load(or_5_out), .D(bit_extender_2_out), .count(AP_CNT), .Q(AP_q), .clk(and_4_out), .clr(RST));  // open: carry
  Counter #(.width(7), .max('h7f)) PC (
    .load(demultiplexer_1_out9), .D(bit_extender_3_out), .count(xor_1_out), .Q(PC_q), .clk(and_4_out),
    .clr(RST));  // open: carry
  RAM #(.addrWidth(7), .dataWidth(16)) ram_1 (
    .addr(multiplexer_1_out), .data(ram_1_data), .clk(and_4_out), .ld(1'b1));  // open: sel, clr
  Counter #(.width(2), .max('h3)) counter_2 (
    .load(PC_CNT), .D(2'b00), .count(not_4_out), .Q(S), .clk(and_4_out), .clr(RST));  // open: carry
  assign {ARIN, controlled_buffer_8_out[7], ABIN, controlled_buffer_8_out[5], RW, RLC, controlled_buffer_8_out[2], RT, controlled_buffer_8_out[0]} = or_6_out ? bit_extender_4_out : 9'bz;  // Controlled_Buffer controlled_buffer_8
  or or_6 (or_6_out, W, RET, LD_ST, ARITH);
  Multiplexer #(.width(7), .disabled(0)) multiplexer_2 (
    .in0(AR1_q), .in1(AR2_q), .out(multiplexer_2_out), .sel(controlled_buffer_4_out[0]), .en(and_1_out));
  \Мини_расческа1  \u_мини_расческа1_1  (
    .in_1(ram_1_data), .out_2(\мини_расческа1_1_out_2 ), .out_3(\мини_расческа1_1_out_3 ));
  or or_7 (RVC, MOV_L, controlled_buffer_8_out[7]);
  Pull_Resistor pull_resistor_3 (.node({ARIN, controlled_buffer_8_out[7], ABIN, controlled_buffer_8_out[5], RW, RLC, controlled_buffer_8_out[2], RT, controlled_buffer_8_out[0]}));
  Divider #(.width(16)) divider_1 (
    .a({OR2_q, OR1_q}), .b(16'ha), .out(divider_1_out), .rem(divider_1_rem));  // open: upper
  Bit_Extender #(.out_width(7)) bit_extender_8 (.in(controlled_buffer_9_out), .out(bit_extender_8_out));
  assign bit_extender_9_out = {{1{1'b0}}, AR1_q};  // Bit_Extender bit_extender_9
  assign bit_extender_10_out = {{1{1'b0}}, AR2_q};  // Bit_Extender bit_extender_10
  assign bit_extender_11_out = {{1{1'b0}}, ASR_q};  // Bit_Extender bit_extender_11
  assign bit_extender_12_out = {{1{1'b0}}, HSP_q};  // Bit_Extender bit_extender_12
  assign bit_extender_13_out = {{1{1'b0}}, AP_q};  // Bit_Extender bit_extender_13
  assign bit_extender_14_out = {{1{1'b0}}, PC_q};  // Bit_Extender bit_extender_14
  Pull_Resistor pull_resistor_4 (.node(pull_resistor_4_node));
  Pull_Resistor pull_resistor_5 (.node(pull_resistor_5_node[0]));
  Subtractor #(.width(7)) subtractor_1 (
    .a(ASR_q), .b(multiplexer_2_out), .out(subtractor_1_out), .bin(pull_resistor_4_node));  // open: bout
  Comparator #(.width(7), .mode("unsigned")) comparator_1 (.a(PC_q), .b(in_7), .eq(comparator_1_eq));  // open: gt, lt
  Register PR1 (.D(\мини_расческа1_1_out_2 ), .en(PC_CNT), .Q(PR1_q), .clk(and_4_out), .clr(RST));
  \Мини_расческа2  \u_мини_расческа2_1  (
    .in_1(PR1_q), .in_2(PR2_q),
    .out_3({OP[15], MEM, READ, COUNT, OP[11], RLEFT, RRIGHT[2:1], FLAG, RDST[3:2], BTYPE}));
  Register PR2 (.D(\мини_расческа1_1_out_3 ), .en(PC_CNT), .Q(PR2_q), .clk(and_4_out), .clr(RST));
  not not_5 (not_5_out, READ);
  Divider #(.width(16)) divider_2 (
    .a(divider_1_out), .b(16'ha), .out(divider_2_out), .rem(divider_2_rem));  // open: upper
  Bit_Extender #(.in_width(16), .out_width(4)) bit_extender_15 (.in(divider_2_rem), .out(bit_extender_15_out));
  Bit_Extender #(.in_width(16), .out_width(4)) bit_extender_16 (.in(divider_1_rem), .out(bit_extender_16_out));
  Register #(.width(7)) CR (.D(bit_extender_8_out), .en(CREN), .Q(CR_q), .clk(and_4_out), .clr(RST));
  Multiplexer #(.select(4), .width(8)) multiplexer_3 (
    .in0(RA_q), .in1(RB_q), .in2(RC_q), .in3(RD_q), .in4(bit_extender_9_out), .in5(bit_extender_10_out),
    .in6(bit_extender_11_out), .in7(bit_extender_12_out), .in8(bit_extender_13_out),
    .in9(bit_extender_14_out), .in10(CROUT), .in14({subtractor_1_out, pull_resistor_5_node[0]}),
    .in15({subtractor_1_out, pull_resistor_5_node[0]}), .out(multiplexer_3_out),
    .sel(controlled_buffer_4_out), .en(or_3_out));  // open: in11, in12, in13
  and and_5 (BP_t, comparator_1_eq, BP);
  and and_6 (and_6_out, not_5_out, RW);
  or or_8 (RDO, and_6_out, controlled_buffer_8_out[2]);
  xor xor_2 (xor_2_out, S[0], READ);
  Demultiplexer #(.disabled(0)) demultiplexer_2 (
    .out0(demultiplexer_2_out0), .out1(AP_CNT), .in(STEP), .sel(FLAG), .en(1'b1));
  Divider #(.width(16)) divider_3 (
    .a(divider_2_out), .b(16'ha), .out(divider_3_out), .rem(divider_3_rem));  // open: upper
  Divider #(.width(16)) divider_4 (
    .a(divider_3_out), .b(16'ha), .out(divider_4_out), .rem(divider_4_rem));  // open: upper
  Bit_Extender #(.in_width(16), .out_width(4)) bit_extender_17 (.in(divider_3_rem), .out(bit_extender_17_out));
  Comparator #(.width(7), .mode("unsigned")) comparator_2 (
    .a(AP_q), .b(CR_q), .gt(comparator_2_gt), .eq(comparator_2_eq));  // open: lt
  nor nor_1 (BL2, RA_q[7], RA_q[6], RA_q[5], RA_q[4], RA_q[3], RA_q[2], RA_q[1]);
  Comparator #(.mode("unsigned")) comparator_3 (
    .a(RB_q), .b(RD_q), .gt(comparator_3_gt), .eq(comparator_3_eq));  // open: lt
  Comparator #(.mode("unsigned")) comparator_4 (
    .a(RA_q), .b(RC_q), .gt(comparator_4_gt), .eq(comparator_4_eq));  // open: lt
  Bit_Extender #(.out_width(3)) bit_extender_18 (.in(multiplexer_3_out), .out(bit_extender_18_out));
  Register ALUBUF (.D(multiplexer_3_out), .en(ABIN), .Q(ALUBUF_q), .clk(and_4_out), .clr(ABRES));
  Multiplexer #(.width(8), .disabled(0)) multiplexer_4 (
    .in0(multiplexer_3_out), .in1(multiplexer_7_out), .out(multiplexer_4_out), .sel(OP[11]), .en(1'b1));
  and and_7 (and_7_out, xor_2_out, COUNT, LD_ST);
  and and_8 (and_8_out, and_7_out, READ);
  and and_9 (and_9_out, READ, STEP);
  Divider #(.width(16)) divider_5 (.a(divider_4_out), .b(16'ha), .rem(divider_5_rem));  // open: out, upper
  Bit_Extender #(.in_width(16), .out_width(4)) bit_extender_19 (.in(divider_5_rem), .out(bit_extender_19_out));
  Bit_Extender #(.in_width(16), .out_width(4)) bit_extender_20 (.in(divider_4_rem), .out(bit_extender_20_out));
  assign CROUT = {{1{1'b0}}, CR_q};  // Bit_Extender bit_extender_21
  or or_9 (BEOA, comparator_2_gt, comparator_2_eq);
  and and_10 (and_10_out, comparator_3_eq, comparator_4_gt);
  assign controlled_buffer_9_out = RDO ? multiplexer_3_out : 8'bz;  // Controlled_Buffer controlled_buffer_9
  assign controlled_inverter_1_out = and_11_out ? ~multiplexer_4_out : 8'bz;  // Controlled_Inverter controlled_inverter_1
  assign controlled_inverter_1_out = not_6_out ? multiplexer_4_out : 8'bz;  // Controlled_Buffer controlled_buffer_10
  not not_6 (not_6_out, and_11_out);
  and and_11 (and_11_out, ARITH, COUNT);
  or or_10 (RDI, MOV_L, and_12_out);
  and and_12 (and_12_out, RW, READ);
  and and_13 (and_13_out, demultiplexer_2_out0, and_9_out);
  Hex_Digit_Display hex_digit_display_1 (.value(controlled_buffer_11_out));  // open: dp
  Hex_Digit_Display hex_digit_display_2 (.value(controlled_buffer_12_out));  // open: dp
  assign controlled_buffer_11_out = OUT_q ? bit_extender_20_out : 4'bz;  // Controlled_Buffer controlled_buffer_11
  assign controlled_buffer_12_out = OUT_q ? bit_extender_19_out : 4'bz;  // Controlled_Buffer controlled_buffer_12
  xor xor_3 (xor_3_out, 1'b0, or_11_out);
  or or_11 (or_11_out, comparator_3_gt, and_10_out);
  nand nand_1 (nand_1_out, comparator_3_eq, comparator_4_eq);
  Pull_Resistor pull_resistor_6 (.node(controlled_buffer_9_out));
  ROM #(.addrWidth(3)) rom_2 (.addr(bit_extender_18_out), .data(controlled_buffer_9_out), .sel(and_3_out));
  or or_12 (or_12_out, B, and_11_out);
  assign controlled_buffer_9_out = ALUOUT ? adder_1_out : 8'bz;  // Controlled_Buffer controlled_buffer_13
  Adder adder_1 (.a(ALUBUF_q), .b(controlled_inverter_1_out), .out(adder_1_out), .cin(or_12_out));  // open: cout
  or or_13 (HSP_CNT, and_7_out, demultiplexer_2_out0);
  or or_14 (HSP_DIR, and_8_out, and_13_out);
  and and_14 (AP_DIR, AP_CNT, and_9_out);
  Hex_Digit_Display hex_digit_display_3 (.value(controlled_buffer_14_out));  // open: dp
  Hex_Digit_Display hex_digit_display_4 (.value(controlled_buffer_15_out));  // open: dp
  assign controlled_buffer_14_out = OUT_q ? bit_extender_15_out : 4'bz;  // Controlled_Buffer controlled_buffer_14
  assign controlled_buffer_15_out = OUT_q ? bit_extender_17_out : 4'bz;  // Controlled_Buffer controlled_buffer_15
  and and_15 (BCMP, xor_3_out, nand_1_out);
  Subtractor subtractor_2 (
    .a(controlled_buffer_9_out), .b(bit_extender_24_out), .out(subtractor_2_out));  // open: bin, bout
  Hex_Digit_Display hex_digit_display_5 (.value(controlled_buffer_16_out));  // open: dp
  assign controlled_buffer_16_out = OUT_q ? bit_extender_16_out : 4'bz;  // Controlled_Buffer controlled_buffer_16
  and and_16 (and_16_out, HSP_CNT, HSP_DIR, LD_ST);
  Bit_Extender #(.out_width(7)) bit_extender_22 (.in(subtractor_2_out), .out(bit_extender_22_out));
  Counter #(.width(7), .max('h7f)) AR (
    .load(ARIN), .D(bit_extender_22_out), .count(ARSTEP), .Q(AR_q), .clk(and_4_out), .clr(RST));  // open: carry
  assign controlled_buffer_9_out = RT ? bit_extender_25_out : 8'bz;  // Controlled_Buffer controlled_buffer_17
  assign bit_extender_23_out = {{1{1'b0}}, {RRIGHT[2:1], FLAG}};  // Bit_Extender bit_extender_23
  or or_15 (or_15_out, S[1], S[0]);
  and and_17 (ARSTEP, or_15_out, W);
  or or_16 (ABRES, A1, B, RST, controlled_buffer_8_out[5]);
  or or_17 (PC_CNT, STEP, MOV_L, B, OUT, NOP, LNK, controlled_buffer_8_out[0]);
  assign bit_extender_24_out = {{7{1'b0}}, and_16_out};  // Bit_Extender bit_extender_24
  Multiplexer #(.width(4), .disabled(0)) multiplexer_5 (
    .in0({RLEFT[0], RRIGHT[2:1], FLAG}), .in1(bit_extender_23_out), .out(RV), .sel(ARITH), .en(1'b1));
  Multiplexer #(.width(4), .disabled(0)) multiplexer_6 (
    .in0({RDST[3:2], BTYPE}), .in1({2'b00, FLAG, S[1]}), .out(RDST_t), .sel(ARSTEP), .en(1'b1));
  Register #(.width(7)) u_RET (.D({RLEFT, RRIGHT[2:1], FLAG}), .en(LNK), .Q(RET_q), .clk(and_4_out), .clr(RST));
  assign bit_extender_25_out = {{1{1'b0}}, RET_q};  // Bit_Extender bit_extender_25
  assign bit_extender_26_out = {{1{1'b0}}, {RLEFT, RRIGHT[2:1], FLAG}};  // Bit_Extender bit_extender_26
  assign bit_extender_27_out = {{5{1'b0}}, {RRIGHT[2:1], FLAG}};  // Bit_Extender bit_extender_27
  or or_18 (ALUOUT, A1, B, controlled_buffer_8_out[7]);
  and and_18 (and_18_out, RW, READ);
  and and_19 (and_19_out, RW, MEM);
  Multiplexer #(.width(8), .disabled(0)) multiplexer_7 (
    .in0(bit_extender_26_out), .in1(bit_extender_27_out), .out(multiplexer_7_out), .sel(ARITH), .en(1'b1));
  RAM #(.addrWidth(7)) ram_2 (
    .addr(AR_q), .data(controlled_buffer_9_out), .sel(and_19_out), .clk(and_4_out), .ld(and_18_out));  // open: clr
  Multiplexer #(.select(2), .disabled(0)) multiplexer_8 (
    .in0(1'b1), .in1(BEOA), .in2(BL2), .in3(BCMP), .out(BTrue), .sel(BTYPE), .en(B));
  not not_7 (not_7_out, READ);
  and and_20 (and_20_out, not_7_out, nor_2_out);
  nor nor_2 (nor_2_out, MEM, OP[15]);
  nor nor_3 (nor_3_out, OP[15], MEM, READ, COUNT);
  not not_8 (not_8_out, MEM);
  not not_9 (not_9_out, READ);
  not not_10 (not_10_out, COUNT);
  not not_11 (not_11_out, OP[15]);
  not not_12 (not_12_out, COUNT);
  not not_13 (not_13_out, OP[11]);
  not not_14 (not_14_out, OP[11]);
  and and_21 (MOV_L, OP[15], not_8_out, not_9_out);
  and and_22 (ARITH, OP[15], not_8_out, READ);
  and and_23 (B, nor_2_out, READ, not_10_out);
  and and_24 (LD_ST, OP[15], MEM);
  and and_25 (W, not_11_out, MEM, not_12_out);
  and and_26 (STEP, not_11_out, MEM, COUNT);
  and and_27 (LNK, nor_2_out, READ, COUNT);
  and and_28 (RET, COUNT, OP[11], and_20_out);
  and and_29 (HLT, COUNT, and_20_out, not_13_out);
  and and_30 (NOP, not_14_out, nor_3_out);
  and and_31 (OUT, OP[11], nor_3_out);

  assign RDST[1:0] = BTYPE;
  assign RRIGHT[0] = FLAG;
  assign RSRC = {RLEFT[0], RRIGHT[2:1], FLAG};
  assign VAL = {RLEFT, RRIGHT[2:1], FLAG};

  // Other names for the same wires on the sheet: F = FLAG;
  //   OP (some bits) = {MEM, READ, COUNT, RLEFT, RRIGHT[2:1], FLAG, RDST[3:2], BTYPE}; CMP = BCMP; EOA = BEOA;
  //   L2 = BL2; CNT = COUNT; RL[3:0] = RLEFT

  // Notes on the sheet:
  //   Lookup Table
  //   contents of rom_1 (hex, n*v repeats v):
  //   2 1 0 0 104 10 11 0 48 91 0 0 1a0 11
  //   Память для команд
  //   End Of Array
  //   Числа Леонарда
  //   BUS
  //   contents of rom_2 (hex, n*v repeats v):
  //   1 1 3 5 9 15 25 41
  //   I
  //   Память для операндов
  //   VAL
endmodule

module \Мини_расческа1  (
  input  [15:0] in_1,
  output [7:0] out_2,
  output [7:0] out_3
);


  assign out_2 = in_1[7:0];
  assign out_3 = in_1[15:8];
endmodule

module \Мини_расческа2  (
  input  [7:0] in_1,
  input  [7:0] in_2,
  output [15:0] out_3
);


  assign out_3 = {in_2, in_1};
endmodule
